# Fritzing sketch Circuit diagram (saved by Fritzing 0.9.2b)
breadboards: 1

parts:
  Q1 = NPN-Transistor [package="TO92 [THT]"]
  R1 = Resistor [tolerance=±5% resistance=1k package=THT]
  LASER = Rectifier Diode [package="Melf DO-213 AA [SMD]"]
  R2 = Resistor [tolerance=±5% resistance=800 package=THT]
  R3 = PHOTOCELL [package=photocell-kit]

nets:
  GND: Q1.E, R2.Pin_1
  N1: Q1.B, R1.Pin_1
  N2: Q1.C, LASER.cathode
  laser control: R1.Pin_0
  3.3V: LASER.anode, R3.P$1
  light level: R2.Pin_0, R3.P$2
